# Fritzing sketch LED (saved by Fritzing 0.9.3b)
breadboards: 1

parts:
  Arduino_UNO = Arduino Uno (Rev3)
  LED1 = LEDs [package=led10mm]
  R1 = Resistor [tolerance=±5% resistance=330 package="0603 [SMD]"]
  LED2 = LEDs [package=led10mm]
  R2 = Resistor [tolerance=±5% resistance=330 package="0603 [SMD]"]
  LED3 = LEDs [package=led10mm]
  R3 = Resistor [tolerance=±5% resistance=330 package="0603 [SMD]"]

nets:
  N1: Arduino_UNO.D10_PWM/SS, LED3.A
  N2: Arduino_UNO.D11_PWM/MOSI, LED2.A
  N3: Arduino_UNO.D12/MISO, LED1.A
  N4: Arduino_UNO.GND, R1.Pin_1, R2.Pin_1, R3.Pin_1
  N5: LED1.C, R1.Pin_0
  N6: LED2.C, R2.Pin_0
  N7: LED3.C, R3.Pin_0

// code stored in the sketch: P1Led.ino
int led1 = 12;
int led2 = 11;
int led3 = 10;

void setup(){
	pinMode(led1, OUTPUT);
	pinMode(led2, OUTPUT);
	pinMode(led3, OUTPUT);
}

void loop(){
	digitalWrite(led1, HIGH);
	digitalWrite(led2, HIGH);
	digitalWrite(led3, HIGH);
	delay(2000);
	digitalWrite(led1, LOW);
	digitalWrite(led2, LOW);
	digitalWrite(led3, LOW);
	delay(1000);
}
